# Fritzing sketch 03_analogCDS (saved by Fritzing 0.9.3b)
breadboards: 1

parts:
  부품1 = Arduino Uno (Rev3)
  R2 = Resistor [tolerance=±5% resistance=220 package=THT]
  LED1 = LED - 5mm [color="Red (633nm)" package="5 mm [THT]"]
  R3 = Photocell (LDR) [package=THT]
  R4 = Resistor [tolerance=±5% resistance=220 package=THT]

nets:
  N1: 부품1.A0, R3.pin_0, R4.Pin_1
  N2: 부품1.D10_PWM/SS, LED1.anode
  N3: 부품1.GND, R2.Pin_0, R3.pin_1
  N4: 부품1.5V, R4.Pin_0
  N5: R2.Pin_1, LED1.cathode
